# Fritzing sketch button (saved by Fritzing 0.9.10b)
breadboards: 1

parts:
  Part1 = Arduino Uno (Rev3) - ICSP
  LED1 = LED - 3mm [color="Red (633nm)" current=0.030 package="3 mm [THT]"]
  R1 = Resistor [tolerance=±5% resistance=220 power=0.25 package=THT]  # not connected
  S1 = Pushbutton [package="[SMD]"]

nets:
  N1: Part1.GND, S1.Pin_3, S1.Pin_4
  N2: Part1.D13/SCK, LED1.anode
  N3: Part1.D7, S1.Pin_1, S1.Pin_2
