# Fritzing sketch rgb_led (saved by Fritzing 0.9.10b)
breadboards: 1

parts:
  Part1 = Arduino Uno (Rev3) - ICSP
  R1 = Resistor [tolerance=±5% resistance=220 power=0.25 package=THT]
  U1 = POT [knob_status=50% power=0.5W package=pot_mammoth]
  LED2 = RGB LED (com. cathode, rgb) [package="5 mm [THT]"]
  R2 = Resistor [tolerance=±5% resistance=4.7k power=0.25 package=THT]
  R3 = Resistor [tolerance=±5% resistance=220 power=0.25 package=THT]

nets:
  N1: Part1.A0, U1.A
  N2: Part1.ICSP_MOSI, Part1.D11_PWM/MOSI, R1.Pin_1
  N3: Part1.D9_PWM, R3.Pin_1
  N4: Part1.D10_PWM/SS, R2.Pin_1
  N5: Part1.5V, U1.E
  N6: Part1.GND, U1.S, LED2.common_cathode
  N7: R1.Pin_0, LED2.red_anode
  N8: LED2.green_anode, R2.Pin_0
  N9: LED2.blue_anode, R3.Pin_0
