# Fritzing sketch pwm_led (saved by Fritzing 0.9.10b)
breadboards: 1

parts:
  Part1 = Arduino Uno (Rev3) - ICSP
  LED1 = LED - 3mm [color="Red (633nm)" current=0.030 package="3 mm [THT]"]
  R1 = Resistor [tolerance=±5% resistance=220 power=0.25 package=THT]  # not connected
  U1 = POT [knob_status=50% power=0.5W package=pot_mammoth]

nets:
  N1: Part1.A0, U1.A
  N2: Part1.ICSP_MOSI, Part1.D11_PWM/MOSI, LED1.anode
  N3: Part1.5V, U1.E
  N4: Part1.GND, U1.S
